# Fritzing sketch FinalAssignmentSchematic1 (saved by Fritzing 0.9.4)
circuit board: 8.46667cm x 5.64444cm
breadboards: 1

parts:
  R1 = Rotary Potentiometer (Small) [maximum_resistance=100kΩ package=THT]
  R3 = Resistor [tolerance=±5% resistance=220 package=THT]
  R4 = Resistor [tolerance=±5% resistance=220 package=THT]
  R5 = Resistor [tolerance=±5% resistance=220 package=THT]
  Part1 = Arduino Uno (Rev3)
  LED1 = RGB LED (com. cathode, rbg) [package="5 mm [THT]"]
  S2 = Pushbutton [package="[SMD]"]
  R6 = Resistor [tolerance=±5% resistance=220 package=THT]

nets (from the pcb view):
  N1: R1.leg1, Part1.D13/SCK, Part1.5V, S2.Pin_3, S2.Pin_4
  N2: R1.wiper, Part1.A0
  N3: R1.leg2, Part1.GND, LED1.common_cathode, R6.Pin_1
  N4: R3.Pin_0, Part1.D11_PWM/MOSI
  N5: R3.Pin_1, LED1.red_anode
  N6: R4.Pin_0, Part1.D10_PWM/SS
  N7: R4.Pin_1, LED1.blue_anode
  N8: R5.Pin_0, Part1.D9_PWM
  N9: R5.Pin_1, LED1.green_anode
  N10: S2.Pin_1, S2.Pin_2, R6.Pin_0

// code stored in the sketch: FinalAssignmentSchematic1.ino

